# Fritzing sketch IR SIGNAL EMULATOR.jpeg (saved by Fritzing 1.0.6)

parts:
  IR1 = TSOP312.., 314.. [package=THT]
  U1 = ESP32-38PinWide [part_number=ESP32-38PinWide]
  S1 = Pushbutton [package="[THT]"]
  S2 = Pushbutton [package="[THT]"]
  S3 = Pushbutton [package="[THT]"]
  LED1 = LEDs [package=led10mm]

nets:
  GND: IR1.GND, U1.GND, S1.Pin_1, S1.Pin_2, S2.Pin_1, S2.Pin_2, S3.Pin_1, S3.Pin_2, LED1.C
  N1: IR1.Vs, U1.3.3
  N2: IR1.Data, U1.GPIO15
  N3: U1.GPIO4, LED1.A
  N4: U1.GPIO18, S1.Pin_4
  N5: U1.GPIO19, S2.Pin_4
  N6: U1.GPIO21, S3.Pin_3, S3.Pin_4

custom parts:
  ESP32-38PinWide: Generic 38-Pin ESP32 with wide format (only access to one side of pins on a breadboard) based on Stephen Lilley's HiLetgo ESP-WROOM-32 ESP32 ESP-32S Development Board.
